# Fritzing sketch build-light (saved by Fritzing 0.9.3b)

parts:
  Q3 = NPN-Transistor [package="SOT-23 [SMD]"]
  Q4 = NPN-Transistor [package="SOT-23 [SMD]"]
  R1 = Resistor [tolerance=±5% resistance=1k package="1206 [SMD]"]
  R2 = Resistor [tolerance=±5% resistance=1k package="1206 [SMD]"]
  R3 = Resistor [tolerance=±5% resistance=1k package="1206 [SMD]"]
  LED1 = LED - 3mm [color="Red (633nm)" package="3 mm [THT]"]
  part = LED - 3mm [color="Yellow (595nm)" package="3 mm [THT]"]
  LED3 = LED - 3mm [color="Green (565nm)" package="3 mm [THT]"]
  Power_plug1 = Power plug [part_number="3.3v DC"]
  Part2 = NRF24L01+ Breakout Board
  Q2 = NPN-Transistor [package="SOT-23 [SMD]"]
  Part1 = Arduino Pro Mini (3.3V)
  Power_plug2 = Power plug [part_number="12v DC"]

nets:
  GND: Q3.2, Q4.2, Power_plug1.GND, Part2.GND, Q2.2, Part1.GND, Power_plug2.GND
  N1: Q3.0, R2.Pin_1
  N2: Q3.1, part.cathode
  N3: Q4.0, R1.Pin_1
  N4: Q4.1, LED3.cathode
  N5: R1.Pin_0, Part1.D3
  N6: R2.Pin_0, Part1.D4
  N7: R3.Pin_0, Part1.D2
  N8: R3.Pin_1, Q2.0
  N9: LED1.cathode, Q2.1
  N10: LED1.anode, part.anode, LED3.anode, Power_plug2.VCC
  VCC: Power_plug1.VCC, Part2.VCC, Part1.VCC
  N11: Part2.CE, Part1.D9
  N12: Part2.CS, Part1.D10
  N13: Part2.SCK, Part1.SCK
  N14: Part2.MOSI, Part1.MOSI
  N15: Part2.MISO, Part1.MISO
